// Logisim project seq1101.circ as structural Verilog: 4 circuits, main circuit main
module main (
);

  wire button_1_out, clock_1_out, detector1101_1__1101_was_detected;

  Clock clock_1 (.out(clock_1_out));
  Button button_1 (.out(button_1_out));
  Detector1101 detector1101_1 (
    .Input(button_1_out), .in_2(clock_1_out), ._1101_Was_Detected(detector1101_1__1101_was_detected));
  LED led_1 (.in(detector1101_1__1101_was_detected));
endmodule

module Detector1101 (
  input  Input,
  input  in_2,
  output _1101_Was_Detected
);

  wire d_ff_1_q, d_ff_2_q, d_ff_3_q, nextstatefunction_1_new_state_0, nextstatefunction_1_new_state_1,
       nextstatefunction_1_new_state_2;

  D_Flip_Flop d_ff_1 (.clk(in_2), .D(nextstatefunction_1_new_state_2), .Q(d_ff_1_q));  // open: Qn, preset, en, reset
  D_Flip_Flop d_ff_2 (.clk(in_2), .D(nextstatefunction_1_new_state_1), .Q(d_ff_2_q));  // open: Qn, preset, en, reset
  D_Flip_Flop d_ff_3 (.clk(in_2), .D(nextstatefunction_1_new_state_0), .Q(d_ff_3_q));  // open: Qn, preset, en, reset
  NextStateFunction nextstatefunction_1 (
    .State_2(d_ff_1_q), .State_1(d_ff_2_q), .State_0(d_ff_3_q), .Input(Input),
    .New_State_2(nextstatefunction_1_new_state_2), .New_State_1(nextstatefunction_1_new_state_1),
    .New_State_0(nextstatefunction_1_new_state_0));
  OutputFunction outputfunction_1 (
    .State_2(d_ff_1_q), .State_1(d_ff_2_q), .State_0(d_ff_3_q), .Detected_1101(_1101_Was_Detected));
endmodule

module OutputFunction (
  input  State_2,
  input  State_1,
  input  State_0,
  output Detected_1101
);


  assign Detected_1101 = State_2;
endmodule

module NextStateFunction (
  input  State_2,
  input  State_1,
  input  State_0,
  input  Input,
  output New_State_2,
  output New_State_1,
  output New_State_0
);

  wire and_1_out, and_2_out, and_3_out, and_4_out, and_6_out, and_7_out, and_8_out, and_9_out, and_10_out,
       not_1_out, not_2_out, not_3_out, not_4_out, not_5_out, not_6_out, or_1_out;

  and and_1 (and_1_out, State_1, State_0);
  not not_1 (not_1_out, State_1);
  and and_2 (and_2_out, not_1_out, State_0);
  and and_3 (and_3_out, State_1, not_2_out);
  not not_2 (not_2_out, State_0);
  not not_3 (not_3_out, Input);
  not not_4 (not_4_out, State_2);
  and and_4 (and_4_out, not_4_out, not_5_out);
  not not_5 (not_5_out, State_0);
  not not_6 (not_6_out, State_0);
  and and_5 (New_State_2, and_1_out, Input);
  and and_6 (and_6_out, and_2_out, Input);
  and and_7 (and_7_out, and_3_out, not_3_out);
  and and_8 (and_8_out, and_4_out, Input);
  and and_9 (and_9_out, State_1, not_6_out);
  or or_1 (or_1_out, and_6_out, and_7_out);
  and and_10 (and_10_out, State_2, Input);
  or or_2 (New_State_0, and_8_out, and_9_out);
  or or_3 (New_State_1, or_1_out, and_10_out);
endmodule
