// Logisim project jrmips.circ as structural Verilog: 6 circuits, main circuit main
module main (
  output [15:0] rs,
  output [15:0] rt_or_Imm
);

  wire BN_out, BP_out, branch_control_1_bn, branch_control_1_bp, branch_control_1_bx, branch_control_1_bz,
       BX_out, BZ_out, Clear_PC__Registers__and_Put_out, Clear_RAM_out, CLOCK_out, control_1_addi,
       control_1_alusrc, control_1_branch, control_1_halt, control_1_memread, control_1_memtoreg,
       control_1_memwrite, control_1_put, control_1_regwrite, control_1_shift, n16_bit_alu_1_zero, not_1_out,
       not_2_out, not_3_out, not_4_out, or_1_out, or_2_out, or_3_out;
  wire [1:0] control_1_aluop0;
  wire [2:0] jump_control_1_output;
  wire [3:0] multiplexer_3_out, register_1_q_2, register_1_q_3;
  wire [7:0] adder_1_out, multiplexer_2_out, multiplexer_4_out, multiplexer_9_out, PC_q, register_1_q;
  wire [15:0] bit_extender_1_out, bit_extender_2_out, bit_extender_3_out, multiplexer_1_out,
       multiplexer_5_out, multiplexer_7_out, multiplexer_8_out, multiplexer_10_out, multiplexer_11_out,
       n16_bit_alu_1_result, ram_1_data, registers_1_read_data_2, rom_1_data, shifter_1_out, shifter_2_out;

  not not_1 (not_1_out, control_1_halt);
  Register PC (
    .D(multiplexer_2_out), .en(not_1_out), .Q(PC_q), .clk(CLOCK_out), .clr(Clear_PC__Registers__and_Put_out));
  Clock CLOCK (.out(CLOCK_out));
  Button Clear_PC__Registers__and_Put (.out(Clear_PC__Registers__and_Put_out));
  LED Halted (.in(control_1_halt));
  Button Clear_RAM (.out(Clear_RAM_out));
  Hex_Digit_Display hex_digit_display_1 (.value(register_1_q_3));  // open: dp
  Adder adder_1 (.a(8'h1), .b(PC_q), .out(adder_1_out));  // open: cin, cout
  Hex_Digit_Display hex_digit_display_2 (.value(register_1_q_2));  // open: dp
  Hex_Digit_Display hex_digit_display_3 (.value(register_1_q[7:4]));  // open: dp
  Register #(.width(16)) register_1 (
    .D(rs), .en(control_1_put), .Q({register_1_q_3, register_1_q_2, register_1_q}), .clk(CLOCK_out),
    .clr(Clear_PC__Registers__and_Put_out));
  assign bit_extender_1_out = {{8{1'b0}}, adder_1_out};  // Bit_Extender bit_extender_1
  ROM #(.dataWidth(16)) rom_1 (.addr(PC_q), .data(rom_1_data), .sel(1'b1));
  Hex_Digit_Display hex_digit_display_4 (.value(register_1_q[3:0]));  // open: dp
  Multiplexer #(.width(16), .enable("false")) multiplexer_1 (
    .in0(multiplexer_11_out), .in1(bit_extender_1_out), .out(multiplexer_1_out),
    .sel(jump_control_1_output[2]));
  Jump_Control jump_control_1 (
    .A(rom_1_data[15]), .B(rom_1_data[14]), .C(rom_1_data[13]), .D(rom_1_data[12]), .Subop(rom_1_data[0]),
    .Output(jump_control_1_output));
  Branch_Control branch_control_1 (
    .A(rom_1_data[15]), .B(rom_1_data[14]), .C(rom_1_data[13]), .D(rom_1_data[12]), .Subop(rom_1_data[0]),
    .BN(branch_control_1_bn), .BP(branch_control_1_bp), .BX(branch_control_1_bx), .BZ(branch_control_1_bz));
  Multiplexer #(.width(8), .enable("false")) multiplexer_2 (
    .in0(multiplexer_9_out), .in1(multiplexer_4_out), .out(multiplexer_2_out), .sel(or_1_out));
  Control control_1 (
    .A(rom_1_data[15]), .B(rom_1_data[14]), .C(rom_1_data[13]), .D(rom_1_data[12]), .Subop(rom_1_data[0]),
    .Halt(control_1_halt), .shift(control_1_shift), .ALUSrc(control_1_alusrc), .MemToReg(control_1_memtoreg),
    .RegWrite(control_1_regwrite), .MemRead(control_1_memread), .MemWrite(control_1_memwrite),
    .Branch(control_1_branch), .ALUOp1(control_1_aluop0[1]), .ALUOp0(control_1_aluop0[0]),
    .Put(control_1_put), .addi(control_1_addi));  // open: RegDst
  or or_1 (or_1_out, jump_control_1_output[0], jump_control_1_output[1], jump_control_1_output[2]);
  Multiplexer #(.width(4), .enable("false")) multiplexer_3 (
    .in0(rom_1_data[4:1]), .in1(registers_1_read_data_2[3:0]), .out(multiplexer_3_out), .sel(rom_1_data[0]));
  Registers registers_1 (
    .Write_Enabled(control_1_regwrite), .Read_Register_1(rom_1_data[11:9]),
    .Read_Register_2(rom_1_data[8:6]), .Write_Register(rom_1_data[11:9]), .Write_Data(multiplexer_1_out),
    .Read_Data_1(rs), .Read_Data_2(registers_1_read_data_2), .Clock(CLOCK_out),
    .Clear(Clear_PC__Registers__and_Put_out));
  Multiplexer #(.select(3), .width(8), .enable("false")) multiplexer_4 (
    .in1(rom_1_data[8:1]), .in2(rs[7:0]), .in4(rom_1_data[8:1]), .out(multiplexer_4_out),
    .sel(jump_control_1_output));  // open: in0, in3, in5, in6, in7
  assign bit_extender_2_out = {{8{1'b0}}, rom_1_data[8:1]};  // Bit_Extender bit_extender_2
  assign bit_extender_3_out = {{8{rom_1_data[8]}}, rom_1_data[8:1]};  // Bit_Extender bit_extender_3
  Multiplexer #(.width(16), .enable("false")) multiplexer_5 (
    .in0(bit_extender_2_out), .in1(bit_extender_3_out), .out(multiplexer_5_out), .sel(control_1_addi));
  Multiplexer #(.width(16), .enable("false")) multiplexer_6 (
    .in0(registers_1_read_data_2), .in1(multiplexer_5_out), .out(rt_or_Imm), .sel(control_1_alusrc));
  Shifter #(.width(16)) shifter_1 (.in(rs), .\dist (multiplexer_3_out), .out(shifter_1_out));
  Shifter #(.width(16), .shift("lr")) shifter_2 (.in(rs), .\dist (multiplexer_3_out), .out(shifter_2_out));
  not not_2 (not_2_out, rs[15]);
  not not_3 (not_3_out, n16_bit_alu_1_zero);
  or or_2 (or_2_out, control_1_memwrite, control_1_memread);
  not not_4 (not_4_out, or_2_out);
  _16_bit_ALU u_16_bit_alu_1 (
    .a(rs), .b(rt_or_Imm), .Operation(control_1_aluop0), .Zero(n16_bit_alu_1_zero),
    .Result(n16_bit_alu_1_result));
  Multiplexer #(.width(16), .enable("false")) multiplexer_7 (
    .in0(shifter_1_out), .in1(shifter_2_out), .out(multiplexer_7_out), .sel(rom_1_data[12]));
  and BN (BN_out, control_1_branch, rs[15], branch_control_1_bn);
  and BP (BP_out, control_1_branch, not_2_out, branch_control_1_bp, not_3_out);
  and BX (BX_out, not_3_out, control_1_branch, branch_control_1_bx);
  and BZ (BZ_out, control_1_branch, branch_control_1_bz, n16_bit_alu_1_zero);
  Multiplexer #(.width(16), .enable("false")) multiplexer_8 (
    .in0(registers_1_read_data_2), .in1(n16_bit_alu_1_result), .out(multiplexer_8_out), .sel(not_4_out));
  Multiplexer #(.width(8), .enable("false")) multiplexer_9 (
    .in0(adder_1_out), .in1(rom_1_data[8:1]), .out(multiplexer_9_out), .sel(or_3_out));
  or or_3 (or_3_out, BN_out, BP_out, BX_out, BZ_out);
  RAM #(.dataWidth(16), .bus("separate")) ram_1 (
    .addr(multiplexer_8_out[7:0]), .din(rs), .data(ram_1_data), .str(control_1_memwrite), .sel(1'b1),
    .clk(CLOCK_out), .ld(control_1_memread), .clr(Clear_RAM_out));
  Multiplexer #(.width(16), .enable("false")) multiplexer_10 (
    .in0(multiplexer_8_out), .in1(ram_1_data), .out(multiplexer_10_out), .sel(control_1_memtoreg));
  Multiplexer #(.width(16), .enable("false")) multiplexer_11 (
    .in0(multiplexer_10_out), .in1(multiplexer_7_out), .out(multiplexer_11_out), .sel(control_1_shift));

  // Notes on the sheet:
  //   Zach Sadler
  //   zps6@pitt.edu
  //   Zach Sadler
  //   zps6@pitt.edu
  //   Zach Sadler
  //   zps6@pitt.edu
  //   Instruction Memory
  //   contents of rom_1 (hex, n*v repeats v):
  //   1fc1 ffe 1901 9fe c800 1001 12 ec19 1901 954 c800 2001 fff 7dc1 c000 9025 1ff ec19 7dc0 e03 ec00
  //   Zach Sadler
  //   zps6@pitt.edu
  //   RAM
  //   Zach Sadler
  //   zps6@pitt.edu
endmodule

module Registers (
  input  Write_Enabled,
  input  [2:0] Read_Register_1,
  input  [2:0] Read_Register_2,
  input  [2:0] Write_Register,
  input  [15:0] Write_Data,
  input  Clock,
  input  Clear,
  output [15:0] Read_Data_1,
  output [15:0] Read_Data_2
);

  wire and_1_out, and_2_out, and_3_out, and_4_out, and_5_out, and_6_out, and_7_out, and_8_out,
       decoder_1_out0, decoder_1_out1, decoder_1_out2, decoder_1_out3, decoder_1_out4, decoder_1_out5,
       decoder_1_out6, decoder_1_out7;
  wire [15:0] _000_q, _001_q, _010_q, _011_q, _100_q, _101_q, _110_q, _111_q;

  Decoder #(.select(3), .enable("false")) decoder_1 (
    .out0(decoder_1_out0), .out1(decoder_1_out1), .out2(decoder_1_out2), .out3(decoder_1_out3),
    .out4(decoder_1_out4), .out5(decoder_1_out5), .out6(decoder_1_out6), .out7(decoder_1_out7),
    .sel(Write_Register));
  and and_1 (and_1_out, Write_Enabled, decoder_1_out7);
  and and_2 (and_2_out, Write_Enabled, decoder_1_out6);
  and and_3 (and_3_out, Write_Enabled, decoder_1_out5);
  and and_4 (and_4_out, Write_Enabled, decoder_1_out4);
  and and_5 (and_5_out, Write_Enabled, decoder_1_out3);
  and and_6 (and_6_out, Write_Enabled, decoder_1_out2);
  and and_7 (and_7_out, Write_Enabled, decoder_1_out1);
  and and_8 (and_8_out, Write_Enabled, decoder_1_out0);
  Register #(.width(16)) _111 (.D(Write_Data), .en(and_1_out), .Q(_111_q), .clk(Clock), .clr(Clear));
  Register #(.width(16)) _110 (.D(Write_Data), .en(and_2_out), .Q(_110_q), .clk(Clock), .clr(Clear));
  Register #(.width(16)) _101 (.D(Write_Data), .en(and_3_out), .Q(_101_q), .clk(Clock), .clr(Clear));
  Register #(.width(16)) _100 (.D(Write_Data), .en(and_4_out), .Q(_100_q), .clk(Clock), .clr(Clear));
  Register #(.width(16)) _011 (.D(Write_Data), .en(and_5_out), .Q(_011_q), .clk(Clock), .clr(Clear));
  Register #(.width(16)) _010 (.D(Write_Data), .en(and_6_out), .Q(_010_q), .clk(Clock), .clr(Clear));
  Register #(.width(16)) _001 (.D(Write_Data), .en(and_7_out), .Q(_001_q), .clk(Clock), .clr(Clear));
  Register #(.width(16)) _000 (.D(Write_Data), .en(and_8_out), .Q(_000_q), .clk(Clock), .clr(Clear));
  Multiplexer #(.select(3), .width(16), .disabled(0), .enable("false")) multiplexer_1 (
    .in0(_000_q), .in1(_001_q), .in2(_010_q), .in3(_011_q), .in4(_100_q), .in5(_101_q), .in6(_110_q),
    .in7(_111_q), .out(Read_Data_1), .sel(Read_Register_1));
  Multiplexer #(.select(3), .width(16), .enable("false")) multiplexer_2 (
    .in0(_000_q), .in1(_001_q), .in2(_010_q), .in3(_011_q), .in4(_100_q), .in5(_101_q), .in6(_110_q),
    .in7(_111_q), .out(Read_Data_2), .sel(Read_Register_2));

  // Notes on the sheet:
  //   This is Lab11 extended to 8 registers
endmodule

module _16_bit_ALU (
  input  [1:0] Operation,
  input  [15:0] a,
  input  [15:0] b,
  output Zero,
  output [15:0] Result
);

  wire or_1_out, subtractor_1_bout;
  wire [15:0] adder_1_out, adder_2_out, AND_out, multiplexer_1_out, NOR_out, subtractor_1_out;

  Adder #(.width(16)) adder_1 (.a(a), .b(b), .out(adder_1_out));  // open: cin, cout
  Subtractor #(.width(16)) subtractor_1 (.a(a), .b(b), .out(subtractor_1_out), .bin(1'b1), .bout(subtractor_1_bout));
  assign AND_out = a & b;  // AND_Gate AND, 16 bits wide
  assign NOR_out = ~(a | b);  // NOR_Gate NOR, 16 bits wide
  Adder #(.width(16)) adder_2 (.a(subtractor_1_out), .b(16'h1), .out(adder_2_out));  // open: cin, cout
  Multiplexer #(.width(16), .enable("false")) multiplexer_1 (
    .in0(subtractor_1_out), .in1(adder_2_out), .out(multiplexer_1_out), .sel(subtractor_1_bout));
  Multiplexer #(.select(2), .width(16), .enable("false")) multiplexer_2 (
    .in0(AND_out), .in1(NOR_out), .in2(adder_1_out), .in3(multiplexer_1_out), .out(Result), .sel(Operation));
  not not_1 (Zero, or_1_out);
  or or_1 (or_1_out, a[0], a[1], a[2], a[3], a[4], a[5], a[6], a[7], a[8], a[9], a[10], a[11], a[12], a[13], a[14], a[15]);

  // Notes on the sheet:
  //   00 is AND, 01 is NOR, 10 is ADD, 11 is SUB
endmodule

module Control (
  input  A,
  input  B,
  input  C,
  input  D,
  input  Subop,
  output RegDst,
  output ALUSrc,
  output MemToReg,
  output RegWrite,
  output MemRead,
  output MemWrite,
  output Branch,
  output ALUOp1,
  output ALUOp0,
  output Halt,
  output Put,
  output addi,
  output shift
);

  wire and_1_out, and_2_out, and_4_out, and_5_out, and_6_out, and_7_out, and_8_out, and_9_out, and_11_out,
       and_12_out, and_13_out, and_14_out, and_15_out, and_16_out, and_17_out, and_20_out, and_21_out,
       and_22_out, and_23_out, and_24_out, and_25_out, and_29_out, and_30_out, not_1_out, not_2_out,
       not_3_out, not_4_out, not_5_out, not_6_out, not_7_out, not_8_out, not_9_out, not_10_out, not_11_out,
       not_12_out, not_13_out, not_14_out, not_15_out, not_16_out, not_17_out, not_18_out, not_19_out,
       not_20_out, not_21_out, not_22_out, not_23_out, not_24_out, not_25_out, not_26_out, not_27_out,
       not_28_out, not_29_out, not_30_out, not_31_out, not_32_out, not_33_out, not_34_out, not_35_out,
       not_36_out, not_37_out, not_38_out, not_39_out, not_40_out, not_41_out, not_42_out, not_43_out,
       not_44_out, not_45_out, not_46_out, not_47_out, not_48_out, not_49_out, not_50_out, not_51_out,
       not_52_out, not_53_out, not_54_out, not_55_out, not_56_out, not_57_out, or_3_out, or_4_out;

  not not_1 (not_1_out, A);
  not not_2 (not_2_out, B);
  not not_3 (not_3_out, A);
  not not_4 (not_4_out, C);
  not not_5 (not_5_out, D);
  not not_6 (not_6_out, A);
  not not_7 (not_7_out, B);
  not not_8 (not_8_out, C);
  not not_9 (not_9_out, D);
  not not_10 (not_10_out, A);
  not not_11 (not_11_out, Subop);
  not not_12 (not_12_out, A);
  not not_13 (not_13_out, C);
  not not_14 (not_14_out, B);
  not not_15 (not_15_out, C);
  not not_16 (not_16_out, Subop);
  not not_17 (not_17_out, C);
  not not_18 (not_18_out, D);
  not not_19 (not_19_out, B);
  not not_20 (not_20_out, C);
  not not_21 (not_21_out, C);
  and and_1 (and_1_out, A, B, C, not_22_out, Subop);
  not not_22 (not_22_out, D);
  and and_2 (and_2_out, A, B, C, not_23_out, not_24_out);
  not not_23 (not_23_out, D);
  not not_24 (not_24_out, Subop);
  not not_25 (not_25_out, Subop);
  and and_3 (MemWrite, B, C, Subop);
  not not_26 (not_26_out, B);
  not not_27 (not_27_out, A);
  not not_28 (not_28_out, C);
  not not_29 (not_29_out, C);
  not not_30 (not_30_out, A);
  not not_31 (not_31_out, C);
  not not_32 (not_32_out, D);
  not not_33 (not_33_out, C);
  not not_34 (not_34_out, D);
  not not_35 (not_35_out, A);
  not not_36 (not_36_out, B);
  not not_37 (not_37_out, B);
  not not_38 (not_38_out, B);
  not not_39 (not_39_out, A);
  not not_40 (not_40_out, B);
  not not_41 (not_41_out, D);
  not not_42 (not_42_out, C);
  not not_43 (not_43_out, D);
  not not_44 (not_44_out, A);
  not not_45 (not_45_out, B);
  not not_46 (not_46_out, C);
  not not_47 (not_47_out, D);
  not not_48 (not_48_out, A);
  not not_49 (not_49_out, C);
  not not_50 (not_50_out, D);
  not not_51 (not_51_out, A);
  not not_52 (not_52_out, C);
  and and_4 (and_4_out, not_1_out, not_2_out);
  and and_5 (and_5_out, not_3_out, not_4_out);
  and and_6 (and_6_out, B, not_5_out);
  and and_7 (and_7_out, not_6_out, not_7_out, not_8_out, not_9_out);
  and and_8 (and_8_out, B, C, D);
  and and_9 (and_9_out, not_10_out, B, C, D);
  not not_53 (not_53_out, and_9_out);
  and and_10 (MemToReg, B, C, D, not_11_out);
  and and_11 (and_11_out, not_12_out, not_13_out);
  and and_12 (and_12_out, not_14_out, C);
  and and_13 (and_13_out, B, not_15_out);
  and and_14 (and_14_out, B, not_16_out);
  not not_54 (not_54_out, and_15_out);
  and and_15 (and_15_out, A, B, not_17_out, not_18_out);
  and and_16 (and_16_out, A, not_19_out, not_20_out);
  not not_55 (not_55_out, and_16_out);
  and and_17 (and_17_out, A, not_21_out, B, D);
  not not_56 (not_56_out, and_2_out);
  and and_18 (MemRead, B, C, D, not_25_out);
  and and_19 (Branch, A, not_26_out);
  and and_20 (and_20_out, not_27_out, not_28_out, not_29_out);
  and and_21 (and_21_out, not_30_out, not_31_out, not_32_out);
  and and_22 (and_22_out, B, not_33_out, not_34_out);
  and and_23 (and_23_out, not_35_out, not_36_out, C, D, Subop);
  and and_24 (and_24_out, not_37_out, D, Subop);
  and and_25 (and_25_out, A, not_38_out);
  and and_26 (Halt, not_39_out, not_40_out, C, not_41_out, Subop);
  and and_27 (Put, A, B, not_42_out, not_43_out);
  and and_28 (addi, not_44_out, not_45_out, not_46_out, not_47_out, Subop);
  and and_29 (and_29_out, not_48_out, B, not_49_out, not_50_out);
  or or_1 (shift, and_29_out, and_30_out);
  and and_30 (and_30_out, not_51_out, B, not_52_out, D);
  or or_2 (RegDst, and_4_out, and_5_out, and_6_out);
  or or_3 (or_3_out, and_7_out, and_8_out);
  and and_31 (ALUSrc, or_3_out, not_53_out);
  or or_4 (or_4_out, and_11_out, and_12_out, and_1_out, and_13_out, and_14_out);
  and and_32 (RegWrite, or_4_out, not_54_out, not_56_out, not_55_out, not_57_out);
  not not_57 (not_57_out, and_17_out);
  or or_5 (ALUOp1, and_20_out, and_21_out, and_22_out);
  or or_6 (ALUOp0, and_23_out, and_24_out, and_25_out);

  // Notes on the sheet:
  //   Note this is not actually used
endmodule

module Branch_Control (
  input  A,
  input  B,
  input  C,
  input  D,
  input  Subop,
  output BN,
  output BP,
  output BX,
  output BZ
);

  wire and_1_out, and_2_out, not_1_out, not_2_out, not_3_out, not_4_out, not_5_out, not_6_out, not_7_out;

  not not_1 (not_1_out, B);
  and and_1 (and_1_out, A, not_1_out, not_2_out, not_3_out);
  not not_2 (not_2_out, C);
  not not_3 (not_3_out, D);
  not not_4 (not_4_out, Subop);
  not not_5 (not_5_out, B);
  and and_2 (and_2_out, A, not_5_out, not_6_out, D);
  not not_6 (not_6_out, C);
  not not_7 (not_7_out, Subop);
  and and_3 (BN, and_1_out, not_4_out);
  and and_4 (BP, and_1_out, Subop);
  and and_5 (BX, and_2_out, not_7_out);
  and and_6 (BZ, and_2_out, Subop);
endmodule

module Jump_Control (
  input  A,
  input  B,
  input  C,
  input  D,
  input  Subop,
  output [2:0] Output
);

  wire and_2_out, not_1_out, not_2_out, not_3_out;

  and and_1 (Output[0], A, B, not_1_out, D);
  not not_1 (not_1_out, C);
  and and_2 (and_2_out, A, B, C, not_2_out);
  not not_2 (not_2_out, D);
  not not_3 (not_3_out, Subop);
  and and_3 (Output[1], and_2_out, not_3_out);
  and and_4 (Output[2], and_2_out, Subop);
endmodule
