// Logisim project working2.circ as structural Verilog: 8 circuits, main circuit main
module main (
  input  [7:0] in_1,
  input  Enable_PC,
  input  Clear_PC,
  input  [1:0] Operation,
  input  A_invert,
  input  B_invert,
  input  Carry_in,
  input  [15:0] A,
  input  [15:0] B,
  output Zero,
  output [15:0] Result,
  output Overflow
);

  wire CLOCK_out, new_16_bit_alu_1_zero;
  wire [7:0] adder_1_out, PC_q;
  wire [15:0] bit_extender_1_out, multiplexer_1_out, new_16_bit_alu_1_result, registers_1_read_data_1,
       registers_1_read_data_2, rom_1_data;

  Register PC (.D(adder_1_out), .en(Enable_PC), .Q(PC_q), .clk(CLOCK_out), .clr(Clear_PC));
  Clock CLOCK (.out(CLOCK_out));
  Adder adder_1 (.a(in_1), .b(PC_q), .out(adder_1_out));  // open: cin, cout
  ROM #(.dataWidth(16)) rom_1 (.addr(PC_q), .data(rom_1_data), .sel(1'b1));
  Registers registers_1 (
    .Read_Register_1(rom_1_data[11:9]), .Read_Register_2(rom_1_data[8:6]), .Write_Register(rom_1_data[11:9]),
    .Read_Data_1(registers_1_read_data_1), .Read_Data_2(registers_1_read_data_2));  // open: Write_Enabled, Write_Data
  assign bit_extender_1_out = {{8{rom_1_data[8]}}, rom_1_data[8:1]};  // Bit_Extender bit_extender_1
  Multiplexer #(.width(16), .enable("false")) multiplexer_1 (
    .in0(registers_1_read_data_2), .in1(bit_extender_1_out), .out(multiplexer_1_out));  // open: sel
  New_16_bit_ALU new_16_bit_alu_1 (
    .a(registers_1_read_data_1), .b(multiplexer_1_out), .Zero(new_16_bit_alu_1_zero),
    .Result(new_16_bit_alu_1_result));  // open: A_Invert, B_Invert, Carry_In, Operation
  _16_bit_ALU ALU (
    .B_invert(B_invert), .A_invert(A_invert), .a(A), .b(B), .Operation(Operation), .Carry_in(Carry_in),
    .Zero(Zero), .Output(Result), .Overflow(Overflow));
  RAM #(.dataWidth(16), .bus("separate")) ram_1 (
    .addr(new_16_bit_alu_1_result[7:0]), .din(registers_1_read_data_2));  // open: data, str, sel, clk, ld, clr

  // Notes on the sheet:
  //   Instruction Memory
  //   00 is AND, 01 is NOR, 10 is ADD, 11 is LESS
  //   Control
  //   Subop
  //   RAM
endmodule

module PC (
);


  // Notes on the sheet:
  //   I add 1 to the PC each time because 16 bits = 2 bytes
endmodule

module Registers (
  input  Write_Enabled,
  input  [2:0] Read_Register_1,
  input  [2:0] Read_Register_2,
  input  [2:0] Write_Register,
  input  [15:0] Write_Data,
  output [15:0] Read_Data_1,
  output [15:0] Read_Data_2
);

  wire and_1_out, and_2_out, and_3_out, and_4_out, and_5_out, and_6_out, and_7_out, and_8_out, Clock_out,
       decoder_1_out0, decoder_1_out1, decoder_1_out2, decoder_1_out3, decoder_1_out4, decoder_1_out5,
       decoder_1_out6, decoder_1_out7;
  wire [15:0] _000_q, _001_q, _010_q, _011_q, _100_q, _101_q, _110_q, _111_q;

  Decoder #(.select(3), .enable("false")) decoder_1 (
    .out0(decoder_1_out0), .out1(decoder_1_out1), .out2(decoder_1_out2), .out3(decoder_1_out3),
    .out4(decoder_1_out4), .out5(decoder_1_out5), .out6(decoder_1_out6), .out7(decoder_1_out7),
    .sel(Write_Register));
  and and_1 (and_1_out, Write_Enabled, decoder_1_out7);
  and and_2 (and_2_out, Write_Enabled, decoder_1_out6);
  and and_3 (and_3_out, Write_Enabled, decoder_1_out5);
  and and_4 (and_4_out, Write_Enabled, decoder_1_out4);
  and and_5 (and_5_out, Write_Enabled, decoder_1_out3);
  and and_6 (and_6_out, Write_Enabled, decoder_1_out2);
  and and_7 (and_7_out, Write_Enabled, decoder_1_out1);
  and and_8 (and_8_out, Write_Enabled, decoder_1_out0);
  Clock Clock (.out(Clock_out));
  Register #(.width(16)) _111 (.D(Write_Data), .en(and_1_out), .Q(_111_q), .clk(Clock_out));  // open: clr
  Register #(.width(16)) _110 (.D(Write_Data), .en(and_2_out), .Q(_110_q), .clk(Clock_out));  // open: clr
  Register #(.width(16)) _101 (.D(Write_Data), .en(and_3_out), .Q(_101_q), .clk(Clock_out));  // open: clr
  Register #(.width(16)) _100 (.D(Write_Data), .en(and_4_out), .Q(_100_q), .clk(Clock_out));  // open: clr
  Register #(.width(16)) _011 (.D(Write_Data), .en(and_5_out), .Q(_011_q), .clk(Clock_out));  // open: clr
  Register #(.width(16)) _010 (.D(Write_Data), .en(and_6_out), .Q(_010_q), .clk(Clock_out));  // open: clr
  Register #(.width(16)) _001 (.D(Write_Data), .en(and_7_out), .Q(_001_q), .clk(Clock_out));  // open: clr
  Register #(.width(16)) _000 (.D(Write_Data), .en(and_8_out), .Q(_000_q), .clk(Clock_out));  // open: clr
  Multiplexer #(.select(3), .width(16), .disabled(0), .enable("false")) multiplexer_1 (
    .in0(_000_q), .in1(_001_q), .in2(_010_q), .in3(_011_q), .in4(_100_q), .in5(_101_q), .in6(_110_q),
    .in7(_111_q), .out(Read_Data_1), .sel(Read_Register_1));
  Multiplexer #(.select(3), .width(16), .enable("false")) multiplexer_2 (
    .in0(_000_q), .in1(_001_q), .in2(_010_q), .in3(_011_q), .in4(_100_q), .in5(_101_q), .in6(_110_q),
    .in7(_111_q), .out(Read_Data_2), .sel(Read_Register_2));

  // Notes on the sheet:
  //   This is Lab11 extended to 8 registers
endmodule

module _16_bit_ALU (
  input  B_invert,
  input  Carry_in,
  input  [1:0] Operation,
  input  A_invert,
  input  [15:0] a,
  input  [15:0] b,
  output Zero,
  output [15:0] Output,
  output Overflow
);

  wire n1_bit_alu_1_carry_out, n1_bit_alu_2_carry_out, n1_bit_alu_3_carry_out, n1_bit_alu_4_carry_out,
       n1_bit_alu_5_carry_out, n1_bit_alu_6_carry_out, n1_bit_alu_7_carry_out, n1_bit_alu_8_carry_out,
       n1_bit_alu_9_carry_out, n1_bit_alu_10_carry_out, n1_bit_alu_11_carry_out, n1_bit_alu_12_carry_out,
       n1_bit_alu_13_carry_out, n1_bit_alu_14_carry_out, n1_bit_alu_15_carry_out, n1_bit_alu_last_one_1_set,
       or_1_out;

  _1_bit_ALU u_1_bit_alu_1 (
    .a(a[0]), .b(b[0]), .Less(n1_bit_alu_last_one_1_set), .A_Invert(A_invert), .B_Invert(B_invert),
    .Carry_In(Carry_in), .Operation(Operation), .Carry_Out(n1_bit_alu_1_carry_out), .Result(Output[0]));
  _1_bit_ALU u_1_bit_alu_2 (
    .a(a[1]), .b(b[1]), .Less(1'b0), .A_Invert(A_invert), .B_Invert(B_invert),
    .Carry_In(n1_bit_alu_1_carry_out), .Operation(Operation), .Carry_Out(n1_bit_alu_2_carry_out),
    .Result(Output[1]));
  _1_bit_ALU u_1_bit_alu_3 (
    .a(a[2]), .b(b[2]), .Less(1'b0), .A_Invert(A_invert), .B_Invert(B_invert),
    .Carry_In(n1_bit_alu_2_carry_out), .Operation(Operation), .Carry_Out(n1_bit_alu_3_carry_out),
    .Result(Output[2]));
  _1_bit_ALU u_1_bit_alu_4 (
    .a(a[3]), .b(b[3]), .Less(1'b0), .A_Invert(A_invert), .B_Invert(B_invert),
    .Carry_In(n1_bit_alu_3_carry_out), .Operation(Operation), .Carry_Out(n1_bit_alu_4_carry_out),
    .Result(Output[3]));
  _1_bit_ALU u_1_bit_alu_5 (
    .a(a[4]), .b(b[4]), .Less(1'b0), .A_Invert(A_invert), .B_Invert(B_invert),
    .Carry_In(n1_bit_alu_4_carry_out), .Operation(Operation), .Carry_Out(n1_bit_alu_5_carry_out),
    .Result(Output[4]));
  _1_bit_ALU u_1_bit_alu_6 (
    .a(a[5]), .b(b[5]), .Less(1'b0), .A_Invert(A_invert), .B_Invert(B_invert),
    .Carry_In(n1_bit_alu_5_carry_out), .Operation(Operation), .Carry_Out(n1_bit_alu_6_carry_out),
    .Result(Output[5]));
  _1_bit_ALU u_1_bit_alu_7 (
    .a(a[6]), .b(b[6]), .Less(1'b0), .A_Invert(A_invert), .B_Invert(B_invert),
    .Carry_In(n1_bit_alu_6_carry_out), .Operation(Operation), .Carry_Out(n1_bit_alu_7_carry_out),
    .Result(Output[6]));
  _1_bit_ALU u_1_bit_alu_8 (
    .a(a[7]), .b(b[7]), .Less(1'b0), .A_Invert(A_invert), .B_Invert(B_invert),
    .Carry_In(n1_bit_alu_7_carry_out), .Operation(Operation), .Carry_Out(n1_bit_alu_8_carry_out),
    .Result(Output[7]));
  _1_bit_ALU u_1_bit_alu_9 (
    .a(a[8]), .b(b[8]), .Less(1'b0), .A_Invert(A_invert), .B_Invert(B_invert),
    .Carry_In(n1_bit_alu_8_carry_out), .Operation(Operation), .Carry_Out(n1_bit_alu_9_carry_out),
    .Result(Output[8]));
  _1_bit_ALU u_1_bit_alu_10 (
    .a(a[9]), .b(b[9]), .Less(1'b0), .A_Invert(A_invert), .B_Invert(B_invert),
    .Carry_In(n1_bit_alu_9_carry_out), .Operation(Operation), .Carry_Out(n1_bit_alu_10_carry_out),
    .Result(Output[9]));
  _1_bit_ALU u_1_bit_alu_11 (
    .a(a[10]), .b(b[10]), .Less(1'b0), .A_Invert(A_invert), .B_Invert(B_invert),
    .Carry_In(n1_bit_alu_10_carry_out), .Operation(Operation), .Carry_Out(n1_bit_alu_11_carry_out),
    .Result(Output[10]));
  _1_bit_ALU u_1_bit_alu_12 (
    .a(a[11]), .b(b[11]), .Less(1'b0), .A_Invert(A_invert), .B_Invert(B_invert),
    .Carry_In(n1_bit_alu_11_carry_out), .Operation(Operation), .Carry_Out(n1_bit_alu_12_carry_out),
    .Result(Output[11]));
  _1_bit_ALU u_1_bit_alu_13 (
    .a(a[12]), .b(b[12]), .Less(1'b0), .A_Invert(A_invert), .B_Invert(B_invert),
    .Carry_In(n1_bit_alu_12_carry_out), .Operation(Operation), .Carry_Out(n1_bit_alu_13_carry_out),
    .Result(Output[12]));
  _1_bit_ALU u_1_bit_alu_14 (
    .a(a[13]), .b(b[13]), .Less(1'b0), .A_Invert(A_invert), .B_Invert(B_invert),
    .Carry_In(n1_bit_alu_13_carry_out), .Operation(Operation), .Carry_Out(n1_bit_alu_14_carry_out),
    .Result(Output[13]));
  _1_bit_ALU u_1_bit_alu_15 (
    .a(a[14]), .b(b[14]), .Less(1'b0), .A_Invert(A_invert), .B_Invert(B_invert),
    .Carry_In(n1_bit_alu_14_carry_out), .Operation(Operation), .Carry_Out(n1_bit_alu_15_carry_out),
    .Result(Output[14]));
  _1_bit_ALU_last_one u_1_bit_alu_last_one_1 (
    .a(a[15]), .b(b[15]), .Less(1'b0), .A_Invert(A_invert), .B_Invert(B_invert),
    .Carry_In(n1_bit_alu_15_carry_out), .Operation(Operation), .Result(Output[15]),
    .Set(n1_bit_alu_last_one_1_set), .Overflow(Overflow));
  or or_1 (or_1_out, Output[0], Output[1], Output[2], Output[3], Output[4], Output[5], Output[6], Output[7], Output[8], Output[9], Output[10], Output[11], Output[12], Output[13], Output[14], Output[15]);
  not not_1 (Zero, or_1_out);

  // Notes on the sheet:
  //   00 is AND, 01 is NOR, 10 is ADD, 11 is LESS
endmodule

module _1_bit_ALU (
  input  A_Invert,
  input  B_Invert,
  input  Carry_In,
  input  [1:0] Operation,
  input  a,
  input  b,
  input  Less,
  output Result,
  output Carry_Out
);

  wire adder_1_out, AND_out, multiplexer_1_out, multiplexer_2_out, NOR_out, not_1_out, not_2_out;

  not not_1 (not_1_out, a);
  not not_2 (not_2_out, b);
  Multiplexer #(.enable("false")) multiplexer_1 (.in0(a), .in1(not_1_out), .out(multiplexer_1_out), .sel(A_Invert));
  Multiplexer #(.enable("false")) multiplexer_2 (.in0(b), .in1(not_2_out), .out(multiplexer_2_out), .sel(B_Invert));
  Adder #(.width(1)) adder_1 (
    .a(multiplexer_1_out), .b(multiplexer_2_out), .out(adder_1_out), .cin(Carry_In), .cout(Carry_Out));
  and AND (AND_out, multiplexer_1_out, multiplexer_2_out);
  nor NOR (NOR_out, multiplexer_1_out, multiplexer_2_out);
  Multiplexer #(.select(2), .enable("false")) multiplexer_3 (
    .in0(AND_out), .in1(NOR_out), .in2(adder_1_out), .in3(Less), .out(Result), .sel(Operation));

  // Notes on the sheet:
  //   00 is AND, 01 is NOR, 10 is ADD, 11 is LESS
endmodule

module _1_bit_ALU_last_one (
  input  A_Invert,
  input  B_Invert,
  input  Carry_In,
  input  [1:0] Operation,
  input  a,
  input  b,
  input  Less,
  output Result,
  output Set,
  output Overflow
);

  wire adder_1_cout, AND_out, multiplexer_1_out, multiplexer_2_out, NOR_out, not_1_out, not_2_out;

  not not_1 (not_1_out, a);
  not not_2 (not_2_out, b);
  Multiplexer #(.enable("false")) multiplexer_1 (.in0(a), .in1(not_1_out), .out(multiplexer_1_out), .sel(A_Invert));
  Multiplexer #(.enable("false")) multiplexer_2 (.in0(b), .in1(not_2_out), .out(multiplexer_2_out), .sel(B_Invert));
  Adder #(.width(1)) adder_1 (
    .a(multiplexer_1_out), .b(multiplexer_2_out), .out(Set), .cin(Carry_In), .cout(adder_1_cout));
  Overflow_Detection overflow_detection_1 (
    .B_invert_over(B_Invert), .A_over(multiplexer_1_out), .B_value_over(multiplexer_2_out),
    .Result_of_add_over(Set), .Carry_out_over(adder_1_cout), .Overflow(Overflow));
  and AND (AND_out, multiplexer_1_out, multiplexer_2_out);
  nor NOR (NOR_out, multiplexer_1_out, multiplexer_2_out);
  Multiplexer #(.select(2), .enable("false")) multiplexer_3 (
    .in0(AND_out), .in1(NOR_out), .in2(Set), .in3(Less), .out(Result), .sel(Operation));

  // Notes on the sheet:
  //   00 is AND, 01 is NOR, 10 is ADD, 11 is LESS
endmodule

module Overflow_Detection (
  input  B_invert_over,
  input  A_over,
  input  B_value_over,
  input  Result_of_add_over,
  input  Carry_out_over,
  output Overflow
);

  wire and_1_out, and_2_out, not_1_out, not_2_out, not_3_out, not_4_out, not_5_out;

  not not_1 (not_1_out, Result_of_add_over);
  not not_2 (not_2_out, B_invert_over);
  not not_3 (not_3_out, A_over);
  not not_4 (not_4_out, B_value_over);
  not not_5 (not_5_out, Carry_out_over);
  and and_1 (and_1_out, B_invert_over, A_over, B_value_over, not_1_out, Carry_out_over);
  and and_2 (and_2_out, not_2_out, not_3_out, not_4_out, Result_of_add_over, not_5_out);
  or or_1 (Overflow, and_1_out, and_2_out);
endmodule

module New_16_bit_ALU (
  input  A_Invert,
  input  B_Invert,
  input  Carry_In,
  input  [1:0] Operation,
  input  [15:0] a,
  input  [15:0] b,
  output Zero,
  output [15:0] Result
);

  wire or_1_out, subtractor_1_bout;
  wire [15:0] adder_1_out, adder_2_out, AND_out, multiplexer_1_out, multiplexer_2_out, multiplexer_3_out,
       NOR_out, not_1_out, not_2_out, subtractor_1_out;

  assign not_1_out = ~a;  // NOT_Gate not_1, 16 bits wide
  assign not_2_out = ~b;  // NOT_Gate not_2, 16 bits wide
  Multiplexer #(.width(16), .enable("false")) multiplexer_1 (
    .in0(a), .in1(not_1_out), .out(multiplexer_1_out), .sel(A_Invert));
  Multiplexer #(.width(16), .enable("false")) multiplexer_2 (
    .in0(b), .in1(not_2_out), .out(multiplexer_2_out), .sel(B_Invert));
  Adder #(.width(16)) adder_1 (
    .a(multiplexer_1_out), .b(multiplexer_2_out), .out(adder_1_out), .cin(Carry_In));  // open: cout
  Subtractor #(.width(16)) subtractor_1 (
    .a(a), .b(multiplexer_2_out), .out(subtractor_1_out), .bin(1'b1), .bout(subtractor_1_bout));
  assign AND_out = multiplexer_1_out & multiplexer_2_out;  // AND_Gate AND, 16 bits wide
  assign NOR_out = ~(multiplexer_1_out | multiplexer_2_out);  // NOR_Gate NOR, 16 bits wide
  Adder #(.width(16)) adder_2 (.a(subtractor_1_out), .b(16'h1), .out(adder_2_out));  // open: cin, cout
  Multiplexer #(.width(16), .enable("false")) multiplexer_3 (
    .in0(subtractor_1_out), .in1(adder_2_out), .out(multiplexer_3_out), .sel(subtractor_1_bout));
  Multiplexer #(.select(2), .width(16), .enable("false")) multiplexer_4 (
    .in0(AND_out), .in1(NOR_out), .in2(adder_1_out), .in3(multiplexer_3_out), .out(Result), .sel(Operation));
  not not_3 (Zero, or_1_out);
  or or_1 (or_1_out, multiplexer_1_out[0], multiplexer_1_out[1], multiplexer_1_out[2], multiplexer_1_out[3], multiplexer_1_out[4], multiplexer_1_out[5], multiplexer_1_out[6], multiplexer_1_out[7], multiplexer_1_out[8], multiplexer_1_out[9], multiplexer_1_out[10], multiplexer_1_out[11], multiplexer_1_out[12], multiplexer_1_out[13], multiplexer_1_out[14], multiplexer_1_out[15]);

  // Notes on the sheet:
  //   00 is AND, 01 is NOR, 10 is ADD, 11 is SUB
endmodule
