// Logisim project working6.circ as structural Verilog: 9 circuits, main circuit main
module main (
  output [15:0] out_1,
  output [15:0] A,
  output [15:0] B
);

  wire and_1_out, Clear_out, Clear_RAM_out, CLOCK_out, conttrol_1_addi, conttrol_1_alusrc, conttrol_1_branch,
       conttrol_1_halt, conttrol_1_memread, conttrol_1_memtoreg, conttrol_1_memwrite, conttrol_1_put,
       conttrol_1_regdst, conttrol_1_regwrite, conttrol_1_shift, new_16_bit_alu_1_zero, not_1_out, or_1_out;
  wire [1:0] conttrol_1_aluop0;
  wire [3:0] multiplexer_1_out, register_1_q_2, register_1_q_3;
  wire [7:0] adder_1_out, PC_q, register_1_q;
  wire [15:0] bit_extender_1_out, bit_extender_2_out, multiplexer_2_out, multiplexer_4_out,
       multiplexer_5_out, multiplexer_6_out, multiplexer_7_out, new_16_bit_alu_1_result,
       registers_1_read_data_2, rom_1_data, shifter_1_out, shifter_2_out;

  not not_1 (not_1_out, conttrol_1_halt);
  Register PC (.D(adder_1_out), .en(not_1_out), .Q(PC_q), .clk(CLOCK_out), .clr(Clear_out));
  Clock CLOCK (.out(CLOCK_out));
  Button Clear (.out(Clear_out));
  LED Halted (.in(conttrol_1_halt));
  Button Clear_RAM (.out(Clear_RAM_out));
  Hex_Digit_Display hex_digit_display_1 (.value(register_1_q_3));  // open: dp
  Adder adder_1 (.a(8'h1), .b(PC_q), .out(adder_1_out));  // open: cin, cout
  Hex_Digit_Display hex_digit_display_2 (.value(register_1_q_2));  // open: dp
  Hex_Digit_Display hex_digit_display_3 (.value(register_1_q[7:4]));  // open: dp
  Register #(.width(16)) register_1 (
    .D(A), .en(conttrol_1_put), .Q({register_1_q_3, register_1_q_2, register_1_q}), .clk(CLOCK_out),
    .clr(Clear_out));
  ROM #(.dataWidth(16)) rom_1 (.addr(PC_q), .data(rom_1_data), .sel(1'b1));
  Hex_Digit_Display hex_digit_display_4 (.value(register_1_q[3:0]));  // open: dp
  LED RegWrite (.in(conttrol_1_regwrite));
  Conttrol conttrol_1 (
    .A(rom_1_data[15]), .B(rom_1_data[14]), .C(rom_1_data[13]), .D(rom_1_data[12]), .Subop(rom_1_data[0]),
    .Halt(conttrol_1_halt), .shift(conttrol_1_shift), .RegDst(conttrol_1_regdst), .ALUSrc(conttrol_1_alusrc),
    .MemToReg(conttrol_1_memtoreg), .RegWrite(conttrol_1_regwrite), .MemRead(conttrol_1_memread),
    .MemWrite(conttrol_1_memwrite), .Branch(conttrol_1_branch), .ALUOp1(conttrol_1_aluop0[1]),
    .ALUOp0(conttrol_1_aluop0[0]), .Put(conttrol_1_put), .addi(conttrol_1_addi));
  Multiplexer #(.width(4), .enable("false")) multiplexer_1 (
    .in0(rom_1_data[4:1]), .in1(registers_1_read_data_2[3:0]), .out(multiplexer_1_out), .sel(rom_1_data[0]));
  Registers registers_1 (
    .Write_Enabled(conttrol_1_regwrite), .Read_Register_1(rom_1_data[11:9]),
    .Read_Register_2(rom_1_data[8:6]), .Write_Register(rom_1_data[11:9]), .Write_Data(multiplexer_7_out),
    .Read_Data_1(A), .Read_Data_2(registers_1_read_data_2), .Clock(CLOCK_out), .Clear(Clear_out));
  assign bit_extender_1_out = {{8{1'b0}}, rom_1_data[8:1]};  // Bit_Extender bit_extender_1
  assign bit_extender_2_out = {{8{rom_1_data[8]}}, rom_1_data[8:1]};  // Bit_Extender bit_extender_2
  Multiplexer #(.width(16), .enable("false")) multiplexer_2 (
    .in0(bit_extender_1_out), .in1(bit_extender_2_out), .out(multiplexer_2_out), .sel(conttrol_1_addi));
  Multiplexer #(.width(16), .enable("false")) multiplexer_3 (
    .in0(registers_1_read_data_2), .in1(multiplexer_2_out), .out(B), .sel(conttrol_1_alusrc));
  Shifter #(.width(16)) shifter_1 (.in(A), .\dist (multiplexer_1_out), .out(shifter_1_out));
  Shifter #(.width(16), .shift("lr")) shifter_2 (.in(A), .\dist (multiplexer_1_out), .out(shifter_2_out));
  or or_1 (or_1_out, conttrol_1_memwrite, conttrol_1_memread);
  New_16_bit_ALU new_16_bit_alu_1 (
    .a(A), .b(B), .Operation(conttrol_1_aluop0), .Zero(new_16_bit_alu_1_zero),
    .Result(new_16_bit_alu_1_result));
  Multiplexer #(.width(16), .enable("false")) multiplexer_4 (
    .in0(shifter_1_out), .in1(shifter_2_out), .out(multiplexer_4_out), .sel(rom_1_data[12]));
  Multiplexer #(.width(16), .enable("false")) multiplexer_5 (
    .in0(new_16_bit_alu_1_result), .in1(registers_1_read_data_2), .out(multiplexer_5_out), .sel(or_1_out));
  and and_1 (and_1_out, conttrol_1_branch, new_16_bit_alu_1_zero);
  RAM #(.dataWidth(16), .bus("separate")) ram_1 (
    .addr(multiplexer_5_out[7:0]), .din(A), .data(out_1), .str(conttrol_1_memwrite), .sel(1'b1),
    .clk(CLOCK_out), .ld(conttrol_1_memread), .clr(Clear_RAM_out));
  Multiplexer #(.width(16), .enable("false")) multiplexer_6 (
    .in0(multiplexer_5_out), .in1(out_1), .out(multiplexer_6_out), .sel(conttrol_1_memtoreg));
  Multiplexer #(.width(16), .enable("false")) multiplexer_7 (
    .in0(multiplexer_6_out), .in1(multiplexer_4_out), .out(multiplexer_7_out), .sel(conttrol_1_shift));

  // Notes on the sheet:
  //   00 is AND, 01 is NOR, 10 is ADD, 11 is SUB
  //   Instruction Memory
  //   contents of rom_1 (hex, n*v repeats v):
  //   403 80b 7501 7f00 ce00 e03 7f01 7d00 cc00 803 c03 7d01 803 c03 7d01 60d 7ec0 ce00 603 7ec0 ce00 2001
  //   Branch
  //   Zero
  //   RAM
endmodule

module PC (
);


  // Notes on the sheet:
  //   I add 1 to the PC each time because 16 bits = 2 bytes
endmodule

module Registers (
  input  Write_Enabled,
  input  [2:0] Read_Register_1,
  input  [2:0] Read_Register_2,
  input  [2:0] Write_Register,
  input  [15:0] Write_Data,
  input  Clock,
  input  Clear,
  output [15:0] Read_Data_1,
  output [15:0] Read_Data_2
);

  wire and_1_out, and_2_out, and_3_out, and_4_out, and_5_out, and_6_out, and_7_out, and_8_out,
       decoder_1_out0, decoder_1_out1, decoder_1_out2, decoder_1_out3, decoder_1_out4, decoder_1_out5,
       decoder_1_out6, decoder_1_out7;
  wire [15:0] _000_q, _001_q, _010_q, _011_q, _100_q, _101_q, _110_q, _111_q;

  Decoder #(.select(3), .enable("false")) decoder_1 (
    .out0(decoder_1_out0), .out1(decoder_1_out1), .out2(decoder_1_out2), .out3(decoder_1_out3),
    .out4(decoder_1_out4), .out5(decoder_1_out5), .out6(decoder_1_out6), .out7(decoder_1_out7),
    .sel(Write_Register));
  and and_1 (and_1_out, Write_Enabled, decoder_1_out7);
  and and_2 (and_2_out, Write_Enabled, decoder_1_out6);
  and and_3 (and_3_out, Write_Enabled, decoder_1_out5);
  and and_4 (and_4_out, Write_Enabled, decoder_1_out4);
  and and_5 (and_5_out, Write_Enabled, decoder_1_out3);
  and and_6 (and_6_out, Write_Enabled, decoder_1_out2);
  and and_7 (and_7_out, Write_Enabled, decoder_1_out1);
  and and_8 (and_8_out, Write_Enabled, decoder_1_out0);
  Register #(.width(16)) _111 (.D(Write_Data), .en(and_1_out), .Q(_111_q), .clk(Clock), .clr(Clear));
  Register #(.width(16)) _110 (.D(Write_Data), .en(and_2_out), .Q(_110_q), .clk(Clock), .clr(Clear));
  Register #(.width(16)) _101 (.D(Write_Data), .en(and_3_out), .Q(_101_q), .clk(Clock), .clr(Clear));
  Register #(.width(16)) _100 (.D(Write_Data), .en(and_4_out), .Q(_100_q), .clk(Clock), .clr(Clear));
  Register #(.width(16)) _011 (.D(Write_Data), .en(and_5_out), .Q(_011_q), .clk(Clock), .clr(Clear));
  Register #(.width(16)) _010 (.D(Write_Data), .en(and_6_out), .Q(_010_q), .clk(Clock), .clr(Clear));
  Register #(.width(16)) _001 (.D(Write_Data), .en(and_7_out), .Q(_001_q), .clk(Clock), .clr(Clear));
  Register #(.width(16)) _000 (.D(Write_Data), .en(and_8_out), .Q(_000_q), .clk(Clock), .clr(Clear));
  Multiplexer #(.select(3), .width(16), .disabled(0), .enable("false")) multiplexer_1 (
    .in0(_000_q), .in1(_001_q), .in2(_010_q), .in3(_011_q), .in4(_100_q), .in5(_101_q), .in6(_110_q),
    .in7(_111_q), .out(Read_Data_1), .sel(Read_Register_1));
  Multiplexer #(.select(3), .width(16), .enable("false")) multiplexer_2 (
    .in0(_000_q), .in1(_001_q), .in2(_010_q), .in3(_011_q), .in4(_100_q), .in5(_101_q), .in6(_110_q),
    .in7(_111_q), .out(Read_Data_2), .sel(Read_Register_2));

  // Notes on the sheet:
  //   This is Lab11 extended to 8 registers
endmodule

module New_16_bit_ALU (
  input  [1:0] Operation,
  input  [15:0] a,
  input  [15:0] b,
  output Zero,
  output [15:0] Result
);

  wire or_1_out, subtractor_1_bout;
  wire [15:0] adder_1_out, adder_2_out, AND_out, multiplexer_1_out, NOR_out, subtractor_1_out;

  Adder #(.width(16)) adder_1 (.a(a), .b(b), .out(adder_1_out));  // open: cin, cout
  Subtractor #(.width(16)) subtractor_1 (.a(a), .b(b), .out(subtractor_1_out), .bin(1'b1), .bout(subtractor_1_bout));
  assign AND_out = a & b;  // AND_Gate AND, 16 bits wide
  assign NOR_out = ~(a | b);  // NOR_Gate NOR, 16 bits wide
  Adder #(.width(16)) adder_2 (.a(subtractor_1_out), .b(16'h1), .out(adder_2_out));  // open: cin, cout
  Multiplexer #(.width(16), .enable("false")) multiplexer_1 (
    .in0(subtractor_1_out), .in1(adder_2_out), .out(multiplexer_1_out), .sel(subtractor_1_bout));
  Multiplexer #(.select(2), .width(16), .enable("false")) multiplexer_2 (
    .in0(AND_out), .in1(NOR_out), .in2(adder_1_out), .in3(multiplexer_1_out), .out(Result), .sel(Operation));
  not not_1 (Zero, or_1_out);
  or or_1 (or_1_out, a[0], a[1], a[2], a[3], a[4], a[5], a[6], a[7], a[8], a[9], a[10], a[11], a[12], a[13], a[14], a[15]);

  // Notes on the sheet:
  //   00 is AND, 01 is NOR, 10 is ADD, 11 is SUB
endmodule

module Control (
  input  A,
  input  B,
  input  C,
  input  D,
  input  Subop,
  output RegDst,
  output ALUsrc,
  output MemtoReg,
  output RegWrite,
  output MemRead,
  output MemWrite,
  output Branch,
  output ALUOp1,
  output ALUOp1_2,
  output Jump,
  output Halt,
  output Put
);

  wire and_4_out, and_5_out, and_9_out, and_10_out, not_1_out, not_2_out, not_3_out, not_4_out, not_5_out,
       not_6_out, not_7_out, not_8_out, not_9_out, not_10_out, not_11_out, not_12_out, not_13_out,
       not_14_out, not_15_out, not_16_out, not_17_out, not_18_out;

  not not_1 (not_1_out, B);
  not not_2 (not_2_out, Subop);
  not not_3 (not_3_out, B);
  and and_1 (ALUsrc, B, C, D);
  and and_2 (MemtoReg, B, C, D);
  not not_4 (not_4_out, Subop);
  not not_5 (not_5_out, Subop);
  and and_3 (MemWrite, B, C, D, Subop);
  not not_6 (not_6_out, B);
  not not_7 (not_7_out, C);
  not not_8 (not_8_out, B);
  not not_9 (not_9_out, C);
  not not_10 (not_10_out, D);
  not not_11 (not_11_out, B);
  not not_12 (not_12_out, D);
  not not_13 (not_13_out, A);
  not not_14 (not_14_out, B);
  not not_15 (not_15_out, D);
  not not_16 (not_16_out, C);
  not not_17 (not_17_out, D);
  and and_4 (and_4_out, not_1_out, not_2_out);
  not not_18 (not_18_out, C);
  and and_5 (and_5_out, not_3_out, D);
  and and_6 (RegWrite, B, C, D, not_4_out);
  and and_7 (MemRead, B, C, D, not_5_out);
  and and_8 (Branch, A, not_6_out, not_7_out);
  or or_1 (ALUOp1, not_8_out, not_9_out, not_10_out);
  and and_9 (and_9_out, A, not_11_out, C, D, Subop);
  and and_10 (and_10_out, A, B, C, not_12_out);
  and and_11 (Halt, not_13_out, not_14_out, C, not_15_out, Subop);
  and and_12 (Put, A, B, not_16_out, not_17_out);
  or or_2 (RegDst, and_4_out, not_18_out, and_5_out, A);
  or or_3 (Jump, and_9_out, and_10_out);
endmodule

module Halt_put (
  input  A,
  input  B,
  input  C,
  input  D,
  input  Subop,
  output Halt,
  output Put
);

  wire not_1_out, not_2_out, not_3_out, not_4_out, not_5_out;

  not not_1 (not_1_out, A);
  not not_2 (not_2_out, B);
  not not_3 (not_3_out, D);
  not not_4 (not_4_out, C);
  not not_5 (not_5_out, D);
  and and_1 (Halt, not_1_out, not_2_out, C, not_3_out, Subop);
  and and_2 (Put, A, B, not_4_out, not_5_out);
endmodule

module Control_2 (
  input  A,
  input  B,
  input  C,
  input  D,
  input  Subop,
  output RegDst,
  output RegWrite,
  output ALUop1,
  output ALUop2
);

  wire and_1_out, and_2_out, and_3_out, and_4_out, and_5_out, and_6_out, not_1_out, not_2_out, not_3_out,
       not_4_out, not_5_out, not_6_out, not_7_out, not_8_out, not_9_out, not_10_out, not_11_out, not_12_out;

  not not_1 (not_1_out, A);
  not not_2 (not_2_out, B);
  not not_3 (not_3_out, A);
  not not_4 (not_4_out, C);
  not not_5 (not_5_out, A);
  not not_6 (not_6_out, B);
  not not_7 (not_7_out, A);
  not not_8 (not_8_out, C);
  not not_9 (not_9_out, A);
  not not_10 (not_10_out, B);
  not not_11 (not_11_out, A);
  not not_12 (not_12_out, C);
  and and_1 (and_1_out, not_1_out, not_2_out, D);
  and and_2 (and_2_out, not_3_out, B, not_4_out);
  and and_3 (and_3_out, not_5_out, not_6_out, D);
  and and_4 (and_4_out, not_7_out, B, not_8_out);
  and and_5 (and_5_out, not_9_out, not_10_out, D);
  and and_6 (and_6_out, not_11_out, B, not_12_out);
  or or_1 (RegDst, and_1_out, and_2_out);
  or or_2 (RegWrite, and_3_out, and_4_out);
  or or_3 (ALUop1, and_5_out, and_6_out);

  assign ALUop2 = 1'b0;
endmodule

module R__I__LW__SW (
  input  A,
  input  B,
  input  C,
  input  D,
  input  Subop,
  output RegDst,
  output ALUSrc,
  output MemToReg,
  output RegWrite,
  output MemRead,
  output MemWrite,
  output Branch,
  output ALUOp1,
  output ALUOp0,
  output Halt,
  output Put
);

  wire and_3_out, and_4_out, and_5_out, and_6_out, and_7_out, and_8_out, and_9_out, and_10_out, and_11_out,
       and_14_out, and_15_out, and_16_out, not_1_out, not_2_out, not_3_out, not_4_out, not_5_out, not_6_out,
       not_7_out, not_8_out, not_9_out, not_10_out, not_11_out, not_12_out, not_13_out, not_14_out,
       not_15_out, not_16_out, not_17_out, not_18_out, not_19_out, not_20_out, not_21_out, not_22_out,
       not_23_out, not_24_out, not_25_out, not_26_out;

  not not_1 (not_1_out, A);
  not not_2 (not_2_out, B);
  not not_3 (not_3_out, A);
  not not_4 (not_4_out, C);
  not not_5 (not_5_out, D);
  not not_6 (not_6_out, A);
  not not_7 (not_7_out, B);
  not not_8 (not_8_out, C);
  not not_9 (not_9_out, D);
  and and_1 (MemToReg, B, C, D);
  not not_10 (not_10_out, A);
  not not_11 (not_11_out, C);
  not not_12 (not_12_out, B);
  not not_13 (not_13_out, C);
  not not_14 (not_14_out, Subop);
  not not_15 (not_15_out, Subop);
  and and_2 (MemWrite, B, C, Subop);
  not not_16 (not_16_out, B);
  not not_17 (not_17_out, A);
  not not_18 (not_18_out, C);
  not not_19 (not_19_out, B);
  not not_20 (not_20_out, D);
  not not_21 (not_21_out, B);
  not not_22 (not_22_out, A);
  not not_23 (not_23_out, B);
  not not_24 (not_24_out, D);
  not not_25 (not_25_out, C);
  not not_26 (not_26_out, D);
  and and_3 (and_3_out, not_1_out, not_2_out);
  and and_4 (and_4_out, not_3_out, not_4_out);
  and and_5 (and_5_out, B, not_5_out);
  and and_6 (and_6_out, not_6_out, not_7_out, not_8_out, not_9_out);
  and and_7 (and_7_out, B, C, D);
  and and_8 (and_8_out, not_10_out, not_11_out);
  and and_9 (and_9_out, not_12_out, C);
  and and_10 (and_10_out, B, not_13_out);
  and and_11 (and_11_out, B, not_14_out);
  and and_12 (MemRead, B, C, D, not_15_out);
  and and_13 (Branch, A, not_16_out);
  and and_14 (and_14_out, not_17_out, not_18_out);
  and and_15 (and_15_out, not_19_out, C);
  and and_16 (and_16_out, B, not_20_out);
  and and_17 (ALUOp0, A, not_21_out);
  and and_18 (Halt, not_22_out, not_23_out, C, not_24_out, Subop);
  and and_19 (Put, A, B, not_25_out, not_26_out);
  or or_1 (RegDst, and_3_out, and_4_out, and_5_out);
  or or_2 (ALUSrc, and_6_out, and_7_out);
  or or_3 (RegWrite, and_8_out, and_9_out, and_10_out, and_11_out);
  or or_4 (ALUOp1, and_14_out, and_15_out, and_16_out);
endmodule

module Conttrol (
  input  A,
  input  B,
  input  C,
  input  D,
  input  Subop,
  output RegDst,
  output ALUSrc,
  output MemToReg,
  output RegWrite,
  output MemRead,
  output MemWrite,
  output Branch,
  output ALUOp1,
  output ALUOp0,
  output Halt,
  output Put,
  output addi,
  output shift
);

  wire and_2_out, and_3_out, and_4_out, and_5_out, and_6_out, and_7_out, and_9_out, and_10_out, and_11_out,
       and_12_out, and_13_out, and_16_out, and_17_out, and_18_out, and_19_out, and_20_out, and_21_out,
       and_25_out, and_26_out, not_1_out, not_2_out, not_3_out, not_4_out, not_5_out, not_6_out, not_7_out,
       not_8_out, not_9_out, not_10_out, not_11_out, not_12_out, not_13_out, not_14_out, not_15_out,
       not_16_out, not_17_out, not_18_out, not_19_out, not_20_out, not_21_out, not_22_out, not_23_out,
       not_24_out, not_25_out, not_26_out, not_27_out, not_28_out, not_29_out, not_30_out, not_31_out,
       not_32_out, not_33_out, not_34_out, not_35_out, not_36_out, not_37_out, not_38_out, not_39_out,
       not_40_out, not_41_out, not_42_out, not_43_out, not_44_out, not_45_out, not_46_out, not_47_out,
       not_48_out, or_3_out, or_4_out;

  not not_1 (not_1_out, A);
  not not_2 (not_2_out, B);
  not not_3 (not_3_out, A);
  not not_4 (not_4_out, C);
  not not_5 (not_5_out, D);
  not not_6 (not_6_out, A);
  not not_7 (not_7_out, B);
  not not_8 (not_8_out, C);
  not not_9 (not_9_out, D);
  not not_10 (not_10_out, A);
  not not_11 (not_11_out, Subop);
  not not_12 (not_12_out, A);
  not not_13 (not_13_out, C);
  not not_14 (not_14_out, B);
  not not_15 (not_15_out, C);
  not not_16 (not_16_out, Subop);
  not not_17 (not_17_out, C);
  not not_18 (not_18_out, D);
  not not_19 (not_19_out, Subop);
  and and_1 (MemWrite, B, C, Subop);
  not not_20 (not_20_out, B);
  not not_21 (not_21_out, A);
  not not_22 (not_22_out, C);
  not not_23 (not_23_out, C);
  not not_24 (not_24_out, A);
  not not_25 (not_25_out, C);
  not not_26 (not_26_out, D);
  not not_27 (not_27_out, C);
  not not_28 (not_28_out, D);
  not not_29 (not_29_out, A);
  not not_30 (not_30_out, B);
  not not_31 (not_31_out, B);
  not not_32 (not_32_out, B);
  not not_33 (not_33_out, A);
  not not_34 (not_34_out, B);
  not not_35 (not_35_out, D);
  not not_36 (not_36_out, C);
  not not_37 (not_37_out, D);
  not not_38 (not_38_out, A);
  not not_39 (not_39_out, B);
  not not_40 (not_40_out, C);
  not not_41 (not_41_out, D);
  not not_42 (not_42_out, A);
  not not_43 (not_43_out, C);
  not not_44 (not_44_out, D);
  not not_45 (not_45_out, A);
  not not_46 (not_46_out, C);
  and and_2 (and_2_out, not_1_out, not_2_out);
  and and_3 (and_3_out, not_3_out, not_4_out);
  and and_4 (and_4_out, B, not_5_out);
  and and_5 (and_5_out, not_6_out, not_7_out, not_8_out, not_9_out);
  and and_6 (and_6_out, B, C, D);
  and and_7 (and_7_out, not_10_out, B, C, D);
  not not_47 (not_47_out, and_7_out);
  and and_8 (MemToReg, B, C, D, not_11_out);
  and and_9 (and_9_out, not_12_out, not_13_out);
  and and_10 (and_10_out, not_14_out, C);
  and and_11 (and_11_out, B, not_15_out);
  and and_12 (and_12_out, B, not_16_out);
  not not_48 (not_48_out, and_13_out);
  and and_13 (and_13_out, A, B, not_17_out, not_18_out);
  and and_14 (MemRead, B, C, D, not_19_out);
  and and_15 (Branch, A, not_20_out);
  and and_16 (and_16_out, not_21_out, not_22_out, not_23_out);
  and and_17 (and_17_out, not_24_out, not_25_out, not_26_out);
  and and_18 (and_18_out, B, not_27_out, not_28_out);
  and and_19 (and_19_out, not_29_out, not_30_out, C, D, Subop);
  and and_20 (and_20_out, not_31_out, D, Subop);
  and and_21 (and_21_out, A, not_32_out);
  and and_22 (Halt, not_33_out, not_34_out, C, not_35_out, Subop);
  and and_23 (Put, A, B, not_36_out, not_37_out);
  and and_24 (addi, not_38_out, not_39_out, not_40_out, not_41_out, Subop);
  and and_25 (and_25_out, not_42_out, B, not_43_out, not_44_out);
  or or_1 (shift, and_25_out, and_26_out);
  and and_26 (and_26_out, not_45_out, B, not_46_out, D);
  or or_2 (RegDst, and_2_out, and_3_out, and_4_out);
  or or_3 (or_3_out, and_5_out, and_6_out);
  and and_27 (ALUSrc, or_3_out, not_47_out);
  or or_4 (or_4_out, and_9_out, and_10_out, and_11_out, and_12_out);
  and and_28 (RegWrite, or_4_out, not_48_out);
  or or_5 (ALUOp1, and_16_out, and_17_out, and_18_out);
  or or_6 (ALUOp0, and_19_out, and_20_out, and_21_out);
endmodule
