// Logisim project lab10part2.circ as structural Verilog
module GrayCode (
  input  [3:0] \input ,
  output X2,
  output X1,
  output X0
);

  wire xor_1_out, xor_2_out, xor_3_out;

  xor xor_1 (xor_1_out, \input [0], \input [1]);
  xor xor_2 (xor_2_out, \input [2], \input [3]);
  xor xor_3 (xor_3_out, xor_1_out, xor_2_out);
  BitAdder #(.width(1)) bitadder_1 (
    .in0(xor_3_out), .in1(\input [3]), .in2(\input [0]), .in3(\input [1]), .in4(\input [2]),
    .out({X2, X1, X0}));
endmodule
