// Logisim project lab11part1.circ as structural Verilog: 1 circuit, main circuit main
module main (
  input  Write_Enabled,
  input  [1:0] Read_Register_2,
  input  [1:0] Read_Register_1,
  input  [1:0] Write_Register,
  input  [15:0] Write_Data,
  output [15:0] Read_Data_1,
  output [15:0] Read_Data_2
);

  wire and_1_out, and_2_out, and_3_out, and_4_out, Clock_out, decoder_1_out0, decoder_1_out1, decoder_1_out2,
       decoder_1_out3;
  wire [15:0] _00_q, _01_q, _10_q, _11_q;

  Decoder #(.select(2), .enable("false")) decoder_1 (
    .out0(decoder_1_out0), .out1(decoder_1_out1), .out2(decoder_1_out2), .out3(decoder_1_out3),
    .sel(Write_Register));
  and and_1 (and_1_out, Write_Enabled, decoder_1_out3);
  and and_2 (and_2_out, Write_Enabled, decoder_1_out2);
  and and_3 (and_3_out, Write_Enabled, decoder_1_out1);
  and and_4 (and_4_out, Write_Enabled, decoder_1_out0);
  Clock Clock (.out(Clock_out));
  Register #(.width(16)) _11 (.D(Write_Data), .en(and_1_out), .Q(_11_q), .clk(Clock_out));  // open: clr
  Register #(.width(16)) _10 (.D(Write_Data), .en(and_2_out), .Q(_10_q), .clk(Clock_out));  // open: clr
  Register #(.width(16)) _01 (.D(Write_Data), .en(and_3_out), .Q(_01_q), .clk(Clock_out));  // open: clr
  Register #(.width(16)) _00 (.D(Write_Data), .en(and_4_out), .Q(_00_q), .clk(Clock_out));  // open: clr
  Multiplexer #(.select(2), .width(16), .disabled(0), .enable("false")) multiplexer_1 (
    .in0(_00_q), .in1(_01_q), .in2(_10_q), .in3(_11_q), .out(Read_Data_1), .sel(Read_Register_1));
  Multiplexer #(.select(2), .width(16), .enable("false")) multiplexer_2 (
    .in0(_00_q), .in1(_01_q), .in2(_10_q), .in3(_11_q), .out(Read_Data_2), .sel(Read_Register_2));
endmodule
