// Logisim project lab11part2.circ as structural Verilog: 1 circuit, main circuit main
module main (
);

  wire Clear_RAM_out, clock_1_out, counter_1_carry, not_1_out, not_2_out, not_3_out, Reset_Counter_out,
       To_get_the_first_one_carry;
  wire [7:0] counter_1_q, ram_1_data;

  Counter #(.max('h1), .ongoal("stay")) To_get_the_first_one (
    .carry(To_get_the_first_one_carry), .clk(clock_1_out), .clr(Reset_Counter_out));  // open: load, D, count, Q
  not not_1 (not_1_out, To_get_the_first_one_carry);
  Counter #(.ongoal("stay")) counter_1 (
    .load(not_1_out), .Q(counter_1_q), .carry(counter_1_carry), .clk(clock_1_out), .clr(Reset_Counter_out));  // open: D, count
  Clock clock_1 (.out(clock_1_out));
  Button Reset_Counter (.out(Reset_Counter_out));
  not not_2 (not_2_out, counter_1_carry);
  not not_3 (not_3_out, clock_1_out);
  RAM #(.bus("asynch")) ram_1 (
    .addr(counter_1_q), .data(ram_1_data), .sel(not_2_out), .ld(not_3_out), .clr(Clear_RAM_out));
  assign ram_1_data = clock_1_out ? 8'h61 : 8'bz;  // Controlled_Buffer controlled_buffer_1
  Button Clear_RAM (.out(Clear_RAM_out));
endmodule
